// Logisim project ALU.circ as structural Verilog: 1 circuit, main circuit main
module main (
  input  [15:0] DR,
  input  [1:0] Eval,
  input  CLK,
  input  [7:0] INPR,
  input  [6:0] INP_7,
  input  Inc,
  input  CLEAR,
  output E,
  output [15:0] AC
);

  wire and_1_out, d_ff_1_qn, main_1_p5, main_2_p5, main_3_p5, main_4_p5, main_5_p5, main_6_p5, main_7_p5,
       main_8_p5, main_9_p5, main_10_p5, main_11_p5, main_12_p5, main_13_p5, main_14_p5, main_15_p5,
       main_16_p5, multiplexer_3_out, multiplexer_4_out, multiplexer_5_out, or_1_out, or_2_out;
  wire [6:0] multiplexer_2_out;
  wire [15:0] multiplexer_1_out;

  or or_1 (or_1_out, 1'b0, multiplexer_2_out[6], multiplexer_2_out[5], multiplexer_2_out[4], multiplexer_2_out[2], multiplexer_2_out[1], multiplexer_2_out[0], multiplexer_2_out[3]);
  Multiplexer #(.width(16)) multiplexer_1 (.in0(DR), .in1(16'h1), .out(multiplexer_1_out), .sel(Inc));  // open: en
  Multiplexer #(.width(7)) multiplexer_2 (
    .in0(INP_7), .in1(7'b0000010), .out(multiplexer_2_out), .sel(Inc));  // open: en
  // Alublock_main main_1: pin names not known; wires that end beside it: multiplexer_1_out[0], AC[1], AC[0], E, main_1_p5, 1'b0, INPR[0], or_1_out, CLK, AC[0], CLEAR
  // Alublock_main main_2: pin names not known; wires that end beside it: multiplexer_1_out[1], AC[2], AC[1], AC[0], main_2_p5, main_1_p5, INPR[1], or_1_out, CLK, AC[1], CLEAR
  // Alublock_main main_3: pin names not known; wires that end beside it: multiplexer_1_out[2], AC[3], AC[2], AC[1], main_3_p5, main_2_p5, INPR[2], or_1_out, CLK, AC[2], CLEAR
  // Alublock_main main_4: pin names not known; wires that end beside it: multiplexer_1_out[3], AC[4], AC[3], AC[2], main_4_p5, main_3_p5, INPR[3], or_1_out, CLK, AC[3], CLEAR
  // Alublock_main main_5: pin names not known; wires that end beside it: multiplexer_1_out[4], AC[5], AC[4], AC[3], main_5_p5, main_4_p5, INPR[4], or_1_out, CLK, AC[4], CLEAR
  // Alublock_main main_6: pin names not known; wires that end beside it: multiplexer_1_out[5], AC[6], AC[5], AC[4], main_6_p5, main_5_p5, INPR[5], or_1_out, CLK, AC[5], CLEAR
  // Alublock_main main_7: pin names not known; wires that end beside it: multiplexer_1_out[6], AC[7], AC[6], AC[5], main_7_p5, main_6_p5, INPR[6], or_1_out, CLK, AC[6], CLEAR
  // Alublock_main main_8: pin names not known; wires that end beside it: multiplexer_1_out[7], AC[8], AC[7], AC[6], main_8_p5, main_7_p5, INPR[7], or_1_out, CLK, AC[7], CLEAR
  // Alublock_main main_9: pin names not known; wires that end beside it: multiplexer_1_out[8], AC[9], AC[8], AC[7], main_9_p5, main_8_p5, 1'b0, or_1_out, CLK, AC[8], CLEAR
  // Alublock_main main_10: pin names not known; wires that end beside it: multiplexer_1_out[9], AC[10], AC[9], AC[8], main_10_p5, main_9_p5, 1'b0, or_1_out, CLK, AC[9], CLEAR
  // Alublock_main main_11: pin names not known; wires that end beside it: multiplexer_1_out[10], AC[11], AC[10], AC[9], main_11_p5, main_10_p5, 1'b0, or_1_out, CLK, AC[10], CLEAR
  // Alublock_main main_12: pin names not known; wires that end beside it: multiplexer_1_out[11], AC[12], AC[11], AC[10], main_12_p5, main_11_p5, 1'b0, or_1_out, CLK, AC[11], CLEAR
  // Alublock_main main_13: pin names not known; wires that end beside it: multiplexer_1_out[12], AC[13], AC[12], AC[11], main_13_p5, main_12_p5, 1'b0, or_1_out, CLK, AC[12], CLEAR
  // Alublock_main main_14: pin names not known; wires that end beside it: multiplexer_1_out[13], AC[14], AC[13], AC[12], main_14_p5, main_13_p5, 1'b0, or_1_out, CLK, AC[13], CLEAR
  // Alublock_main main_15: pin names not known; wires that end beside it: multiplexer_1_out[14], AC[15], AC[14], AC[13], main_15_p5, main_14_p5, 1'b0, or_1_out, CLK, AC[14], CLEAR
  // Alublock_main main_16: pin names not known; wires that end beside it: multiplexer_1_out[15], E, AC[15], AC[14], main_16_p5, main_15_p5, 1'b0, or_1_out, CLK, AC[15], CLEAR
  Multiplexer multiplexer_3 (
    .in0(multiplexer_4_out), .in1(and_1_out), .out(multiplexer_3_out), .sel(Eval[0]));  // open: en
  Multiplexer multiplexer_4 (
    .in0(multiplexer_5_out), .in1(AC[0]), .out(multiplexer_4_out), .sel(multiplexer_2_out[5]));  // open: en
  Multiplexer multiplexer_5 (
    .in0(main_16_p5), .in1(AC[15]), .out(multiplexer_5_out), .sel(multiplexer_2_out[6]));  // open: en
  D_Flip_Flop d_ff_1 (
    .clk(CLK), .D(multiplexer_3_out), .Q(E), .Qn(d_ff_1_qn), .en(or_2_out), .reset(Eval[1]));  // open: preset
  and and_1 (and_1_out, d_ff_1_qn, Eval[0]);
  or or_2 (or_2_out, Eval[0], multiplexer_2_out[5], multiplexer_2_out[6]);
endmodule
